# Fritzing sketch vending_machine_actuator (saved by Fritzing 0.9.5d)
breadboards: 2

parts:
  M1 = ESP32-S3-DevKitC-1-N8R8-v1 [part_number=ESP32-S3-DevKitC-1-N8R8-v1]
  SM1 = 28BYJ-48 Stepper Motor [part_number=28BYJ-48]
  Driver1 = 28BYJ-48 Driver Module [part_number=ULN2003 package=THT]
  BAT1 = BC9VPC [package=bc9vpc]

nets:
  N1: M1.pin_1, M1.pin_2
  N2: M1.pin_16, Driver1.IN4
  N3: M1.pin_17, Driver1.IN3
  N4: M1.pin_18, Driver1.IN2
  N5: M1.pin_19, Driver1.IN1
  N6: M1.pin_22, M1.pin_23, M1.pin_24, M1.pin_44, Driver1.GND
  N7: SM1.blue-pin, Driver1.blue-pin
  N8: SM1.pink-pin, Driver1.pink-pin
  N9: SM1.yellow-pin, Driver1.yellow-pin
  N10: SM1.orange-pin, Driver1.orange-pin
  N11: SM1.red-pin, Driver1.red-pin
  N12: Driver1.Vmotor, BAT1.V+

custom parts:
  ESP32-S3-DevKitC-1-N8R8-v1: ESP32-S3-DevKitC-1-N8R8-v1 This module is 44pins long (2x22) and 11 pins width.
  28BYJ-48 Stepper Motor: Unipolar Stepper Motor 28BYJ-48 Top coil - pink & orange Bottom coil - blue & yellow Common rail - red Connector pins: blue - pink - yellow - orange - red
  28BYJ-48 Driver Module: Generic male header
